# Fritzing sketch DevreŞeması (saved by Fritzing 0.9.3b)
breadboards: 2

parts:
  J1 = Piezo Speaker
  R2 = Resistor [tolerance=±5% resistance=220 package="1206 [SMD]"]
  R3 = Resistor [tolerance=±5% resistance=220 package="1206 [SMD]"]
  LCD1 = LCD screen
  LCM1602_IIC1 = LCM1602 IIC [part_number="LCM1602 IIC" chip_label="LCM1602 IIC" package="DIP (Dual Inline) [THT]"]
  LED2 = smd LED [color="Red (633nm)" package="1206 [SMD]"]
  LED3 = smd LED [color="Green (555nm)" package="1206 [SMD]"]
  LED4 = smd LED [color="Green (555nm)" package="1206 [SMD]"]
  LED5 = smd LED [color="Green (555nm)" package="1206 [SMD]"]
  R1 = Resistor [tolerance=±5% resistance=220 package="1206 [SMD]"]
  R4 = Resistor [tolerance=±5% resistance=220 package="1206 [SMD]"]
  hc-sr1 = hc-sr04
  U3 = ESP8266 NodeMCU LoLin module
  KF-1 = KF-301 Relay [package=THT]
  U4 = LIPO-110mAh [package=lipo-110]
  WATER_PUMP1 = water pump/motor  # not connected

nets:
  GND: J1.pin2, LCM1602_IIC1.GND, hc-sr1.GND
  N1: R2.Pin_1, LED5.cathode
  N2: R3.Pin_1, LED3.cathode
  VSS: LCD1.VSS, LCM1602_IIC1.VSS
  VDD: LCD1.VDD, LCM1602_IIC1.VDD
  N3: LCD1.V0, LCM1602_IIC1.V0
  N4: LCD1.RS, LCM1602_IIC1.RS
  N5: LCD1.R/W, LCM1602_IIC1.RW
  N6: LCD1.E, LCM1602_IIC1.E
  N7: LCD1.DB0, LCM1602_IIC1.D0
  N8: LCD1.DB1, LCM1602_IIC1.D1
  N9: LCD1.DB2, LCM1602_IIC1.D2
  N10: LCD1.DB3, LCM1602_IIC1.D3
  N11: LCD1.DB4, LCM1602_IIC1.D4
  N12: LCD1.DB5, LCM1602_IIC1.D5
  N13: LCD1.DB6, LCM1602_IIC1.D6
  N14: LCD1.DB7, LCM1602_IIC1.D7
  N15: LCD1.LED+, LCM1602_IIC1.A
  N16: LCD1.LED-, LCM1602_IIC1.K
  VCC: LCM1602_IIC1.VCC, hc-sr1.VCC, U3.Vin
  N17: LED2.cathode, R1.Pin_1
  N18: LED2.anode, LED3.anode, LED4.anode, LED5.anode
  N19: LED4.cathode, R4.Pin_1
  N20: KF-1.power, U4.+
  N21: KF-1.ground, KF-1.NO, U4.-

custom parts:
  LCM1602 IIC: I2C-Module to use a 1602 or 2004 LCD on with the wire.h libory Serial LCD Modul
  ESP8266 NodeMCU LoLin module: ESP8266 based NodeMCU
  KF-301 Relay: KF-301
  water pump/motor: WATER PUMP BY ARDUBLOCKTR
